# Fritzing sketch pwm (saved by Fritzing 0.8.3b)
circuit board: 10cm x 5cm
breadboards: 1

parts:
  U1 = 555 Timer [package="DIP8 [THT]"]
  C3 = Electrolytic Capacitor [capacitance=10µF package="100 mil [THT, electrolytic]"]
  D2 = Rectifier Diode [part_number=1n4148 breakdown_voltage=3.6V package="300 mil [THT]"]
  R2 = Resistor [tolerance=±5% resistance=100 package=THT]
  R4 = Resistor [tolerance=±5% resistance=100 package=THT]
  R5 = Resistor [tolerance=±5% resistance=100 package=THT]
  C2 = Electrolytic Capacitor [capacitance=1µF package="100 mil [THT, electrolytic]"]
  C4 = Electrolytic Capacitor [capacitance=47µF package="100 mil [THT, electrolytic]"]
  D3 = Rectifier Diode [part_number=1n4148 package="300 mil [THT]"]
  U2 = 555 Timer [package="DIP8 [THT]"]
  D4 = Rectifier Diode [part_number=1n4148 package="300 mil [THT]"]
  D5 = Rectifier Diode [part_number=1n4148 breakdown_voltage=3.6V package="300 mil [THT]"]
  R8 = Resistor [tolerance=±5% resistance=100 package=THT]
  R9 = Resistor [tolerance=±5% resistance=100 package=THT]
  R10 = Resistor [tolerance=±5% resistance=100 package=THT]
  R12 = Resistor [tolerance=±20% resistance=1k package=THT]
  R13 = Resistor [tolerance=±5% resistance=4.7k package=THT]
  Q1 = Basic FET N-Channel [package="TO220 [THT]"]
  D6 = Rectifier Diode [part_number=1N4001 package="300 mil [THT]"]
  R1 = Rotary Potentiometer (Large) [package=THT]
  J1 = Screw terminal - 2 pins [package=THT]
  J2 = female pin header, 3 pins [form="♀ (female)"]
  J3 = male pin header, 1 pin [form="♂ (male)"]
  J4 = female pin header, 3 pins [form="♀ (female)"]
  J5 = male pin header, 1 pin [form="♂ (male)"]
  J6 = screw terminal, 2 pins
  J7 = female pin header, 1 pin [form="♀ (female)"]
  J8 = female pin header, 1 pin [form="♀ (female)"]
  100nF = Capacitor [package=cap-pth-large]
  220nF = Capacitor [package=cap-pth-large]
  10nF = Capacitor [package=cap-pth-large]
  10nF_2 = Capacitor [package=cap-pth-large]
  C5 = Tantalum Capacitor [capacitance=0.1mF package="200 mil [THT, tantalum]"]
  C10 = Tantalum Capacitor [capacitance=0.1mF package="200 mil [THT, tantalum]"]
  10nF_3 = Capacitor [package=cap-pth-large]
  R14 = Rotary Potentiometer (Large) [package=THT]
  R15 = Rotary Potentiometer (Large) [package=THT]
  R16 = Rotary Potentiometer (Large) [package=THT]

nets:
  N1: U1.Ground, U2.Ground, R13.Pin_1, Q1.source, J3.pin1, J5.pin1, J6.pin2, J8.pin1, 10nF.2, 10nF_2.2, C5.-, C10.-
  N2: U1.Trigger, U1.Threshold, C3.+, D2.anode, C2.+, C4.+, D3.cathode
  N3: U1.Output, U2.Reset
  N4: U1.Reset, U1.Vcc_Supply_Voltage, R4.Pin_0, R5.Pin_1, C5.+
  N5: U1.Control_Voltage, 10nF.1
  N6: U1.Discharge, R2.Pin_0, D3.anode, R14.leg1
  N7: C3.-, J4.pin2
  N8: D2.cathode, R1.leg2
  N9: R2.Pin_1, R1.wiper
  N10: R4.Pin_1, R14.wiper
  N11: R5.Pin_0, R8.Pin_0, D6.cathode, J1.pin1, J6.pin1
  N12: C2.-, J4.pin1
  N13: C4.-, J4.pin3
  N14: U2.Trigger, U2.Threshold, D4.cathode, D5.anode, 100nF.1, 220nF.1, 10nF_3.1
  N15: U2.Output, R12.Pin_0
  N16: U2.Control_Voltage, 10nF_2.1
  N17: U2.Discharge, D4.anode, R10.Pin_0, R16.leg1
  N18: U2.Vcc_Supply_Voltage, R8.Pin_1, R9.Pin_0, C10.+
  N19: D5.cathode, R15.leg2
  N20: R9.Pin_1, R16.wiper
  N21: R10.Pin_1, R15.wiper
  N22: R12.Pin_1, R13.Pin_0, Q1.gate, J7.pin1
  N23: Q1.drain, D6.anode, J1.pin2
  N24: J2.pin1, 220nF.2
  N25: J2.pin2, 100nF.2
  N26: J2.pin3, 10nF_3.2
